# Fritzing sketch KnightRider (saved by Fritzing 0.9.0b)
breadboards: 1

parts:
  Parte1 = Arduino Yun
  R1 = Resistor [tolerance=±5% resistance=1k package=THT]
  LED13 = smd LED [color="Red (633nm)" package="0805 [SMD]"]
  R2 = Resistor [tolerance=±5% resistance=1k package=THT]
  R3 = Resistor [tolerance=±5% resistance=1k package=THT]
  R4 = Resistor [tolerance=±5% resistance=1k package=THT]
  LED12 = smd LED [color="Red (633nm)" package="0805 [SMD]"]
  LED8 = smd LED [color="Red (633nm)" package="0805 [SMD]"]
  LED4 = smd LED [color="Red (633nm)" package="0805 [SMD]"]
  S1 = Momentary Switch [package=ksa_sealed_tac_switch]
  S2 = Momentary Switch [package=ksa_sealed_tac_switch]

nets:
  N1: Parte1.D8, R3.Pin_0
  N2: Parte1.D12/MISO, R2.Pin_0
  N3: Parte1.D13/SCK, R1.Pin_0
  N4: Parte1.D2, S1.3
  N5: Parte1.D4, R4.Pin_0
  N6: Parte1.D7, S2.1
  N7: R1.Pin_1, LED13.anode
  N8: LED13.cathode, LED12.cathode, LED8.cathode, LED4.cathode
  N9: R2.Pin_1, LED12.anode
  N10: R3.Pin_1, LED8.anode
  N11: R4.Pin_1, LED4.anode
