# Fritzing sketch KnightRider (saved by Fritzing 0.9.0b)
breadboards: 1

parts:
  Parte1 = Arduino Yun
  R1 = Resistor [tolerance=±5% resistance=1k package=THT]
  LED13 = smd LED [color="Red (633nm)" package="0805 [SMD]"]
  R2 = Resistor [tolerance=±5% resistance=1k package=THT]
  R3 = Resistor [tolerance=±5% resistance=1k package=THT]
  R4 = Resistor [tolerance=±5% resistance=1k package=THT]
  LED12 = smd LED [color="Red (633nm)" package="0805 [SMD]"]
  LED8 = smd LED [color="Red (633nm)" package="0805 [SMD]"]
  LED4 = smd LED [color="Red (633nm)" package="0805 [SMD]"]
  S1 = Momentary Switch [package=ksa_sealed_tac_switch]
  S2 = Momentary Switch [package=ksa_sealed_tac_switch]
  R5 = Resistor [tolerance=±5% resistance=1k package=THT]
  R6 = Resistor [tolerance=±5% resistance=1k package=THT]

nets:
  N1: Parte1.5V, S1.2, S2.2
  N2: Parte1.GND, R5.Pin_0, R6.Pin_0
  N3: Parte1.D8, R3.Pin_0
  N4: Parte1.D12/MISO, R2.Pin_0
  N5: Parte1.D13/SCK, R1.Pin_0
  N6: Parte1.D2, S1.3
  N7: Parte1.D4, R4.Pin_0
  N8: Parte1.D7, S2.3
  N9: R1.Pin_1, LED13.anode
  N10: LED13.cathode, LED12.cathode, LED8.cathode, LED4.cathode
  N11: R2.Pin_1, LED12.anode
  N12: R3.Pin_1, LED8.anode
  N13: R4.Pin_1, LED4.anode
  N14: S1.4, R5.Pin_1
  N15: S2.4, R6.Pin_1
