# Fritzing sketch Ultrasonic-NTC (saved by Fritzing 0.9.0b)
breadboards: 1

parts:
  Parte1 = Arduino Yun
  R1 = Temperature Sensor (Thermistor) [thermistor_type=NTC package=THT]
  R2 = Resistor [tolerance=±5% resistance=1k package="1206 [SMD]"]
  Parte2 = SRF05 Ultrasonic Rangefinder

nets:
  N1: Parte1.A3, R1.pin_1, R2.Pin_1
  N2: Parte1.D2, Parte2.Echo
  N3: Parte1.D4, Parte2.Trig
  5V: Parte1.5V, R2.Pin_0, Parte2.VCC
  GND: Parte1.GND, R1.pin_0, Parte2.GND
