# Fritzing sketch Conexión NTC-Led-Arduino (saved by Fritzing 0.9.0b)
breadboards: 1

parts:
  Parte1 = Arduino Uno (Rev3)
  R2 = Temperature Sensor (Thermistor) [thermistor_type=NTC package=THT]
  R3 = Resistor [tolerance=±5% resistance=1k package="1206 [SMD]"]
  R4 = Resistor [tolerance=±5% resistance=1k package="1206 [SMD]"]
  LED1 = LED - 3mm [color="Red (633nm)" package="3 mm [THT]"]

nets:
  N1: Parte1.A0, R2.pin_0, R3.Pin_1
  N2: Parte1.D2, R4.Pin_0
  N3: Parte1.5V, R3.Pin_0
  N4: Parte1.GND, R2.pin_1, LED1.cathode
  N5: R4.Pin_1, LED1.anode
